# Fritzing sketch InnovationAward (saved by Fritzing 0.8.7b)
circuit board: 8.46667cm x 5.64444cm

parts:
  TRINKET1 = Trinket 5V  # not connected
  C1 = Electrolytic Capacitor [capacitance=1000µF package="300 mil [THT, electrolytic]"]  # not connected
  proto1 = Adafruit_PermaProto_1_4_Board
  NEOPIXEL1 = Neopixel Strip -- White (60/m)
  R1 = Resistor [tolerance=±5% resistance=400 package=THT]  # not connected
  NEOPIXEL2 = Neopixel Strip -- White (60/m)
  RGB_SMD_LED1 = SMD RGB LED (WS2812) [package=5050]
  RGB_SMD_LED2 = SMD RGB LED (WS2812) [package=5050]
  RGB_SMD_LED3 = SMD RGB LED (WS2812) [package=5050]
  RGB_SMD_LED4 = SMD RGB LED (WS2812) [package=5050]
  JACK2 = 2.1mm DC Barrel Jack

nets:
  N1: proto1.connectorA7, proto1.connectorW7
  N2: proto1.connectorA8, proto1.connectorX7
  N3: proto1.connectorA15, RGB_SMD_LED3.DIn
  N4: proto1.connectorW1, JACK2.center
  N5: proto1.connectorW15, NEOPIXEL1.DI, NEOPIXEL2.DI, RGB_SMD_LED3.VDD
  N6: proto1.connectorX1, JACK2.sleeve
  GND: proto1.connectorX13, NEOPIXEL1.GND, NEOPIXEL2.GND, RGB_SMD_LED4.VSS
  +5V: NEOPIXEL1.+5V, NEOPIXEL2.+5V, RGB_SMD_LED4.DOut
  N7: RGB_SMD_LED1.DOut, RGB_SMD_LED2.DIn
  N8: RGB_SMD_LED1.DIn, RGB_SMD_LED3.DOut
  VDD: RGB_SMD_LED1.VDD, RGB_SMD_LED3.VSS
  VSS: RGB_SMD_LED1.VSS, RGB_SMD_LED2.VDD
  N9: RGB_SMD_LED2.DOut, RGB_SMD_LED4.DIn
  VSS_2: RGB_SMD_LED2.VSS, RGB_SMD_LED4.VDD

notes:
  1
  2
  3
  4
  5
  6
  7
  n
  LAMP
  SPIRE 1
  SPIRE 2
  CONTROLLER BOARD
  POWER
  These NeoPixels are not the actual ones which can be connected serially
  Use male and female headers to connect the power & ground buses and the signal line to the power input and NeoPixels

custom parts:
  Trinket 5V: Adafruit Trinket 5V
  Neopixel Strip -- White (60/m): Neopixel Strip, White, 60 pixels per meter.
  2.1mm DC Barrel Jack: 2.1mm DC Barrel Jack with Thru-Hole Connectors (breadboardable)
